// Logisim project first-version.circ as structural Verilog: 3 circuits, main circuit main
module main (
  input  A3,
  input  A2,
  input  A1,
  input  A0,
  input  in_5,
  input  B3,
  input  B2,
  input  B1,
  input  B0,
  output S3,
  output S2,
  output S1,
  output S0,
  output COUT
);

  wire soma_2_cout, soma_3_cout, soma_4_cout, xor_1_out, xor_2_out, xor_3_out, xor_4_out;

  xor xor_1 (xor_1_out, in_5, B3);
  SOMA soma_1 (.A(A3), .B(xor_1_out), .CIN(soma_3_cout), .S(S3), .COUT(COUT));
  xor xor_2 (xor_2_out, in_5, B1);
  xor xor_3 (xor_3_out, in_5, B2);
  SOMA soma_2 (.A(A1), .B(xor_2_out), .CIN(soma_4_cout), .S(S1), .COUT(soma_2_cout));
  SOMA soma_3 (.A(A2), .B(xor_3_out), .CIN(soma_2_cout), .S(S2), .COUT(soma_3_cout));
  xor xor_4 (xor_4_out, in_5, B0);
  SOMA soma_4 (.A(A0), .B(xor_4_out), .CIN(in_5), .S(S0), .COUT(soma_4_cout));

  // Notes on the sheet:
  //   4
  //   8
  //   2
  //   1
  //   8
  //   4
  //   8
  //   2
  //   4
  //   2
  //   1
  //   1
endmodule

module PRIMARY (
  input  A,
  input  B,
  output S,
  output C
);

  xor xor_1 (S, A, B);
  and and_1 (C, A, B);
endmodule

module SOMA (
  input  A,
  input  B,
  input  CIN,
  output S,
  output COUT
);

  wire primary_1_c, primary_1_s, primary_2_c;

  PRIMARY primary_1 (.A(A), .B(B), .S(primary_1_s), .C(primary_1_c));
  PRIMARY primary_2 (.A(primary_1_s), .B(CIN), .S(S), .C(primary_2_c));
  or or_1 (COUT, primary_1_c, primary_2_c);
endmodule
